// Logisim project trab.circ as structural Verilog: 3 circuits, main circuit main
module main (
);

  wire CLK, CONTROL_UNIT_add, CONTROL_UNIT_movacc, CONTROL_UNIT_movreg, CONTROL_UNIT_rdm,
       controlled_buffer_1_out, HLT, not_1_out, not_2_out, not_3_out, RESETALL, STR;
  wire [1:0] CONTROL_UNIT_regaddr0, CONTROL_UNIT_regaddr1, RAMADDR;
  wire [4:0] counter_1_q;
  wire [7:0] ram_1_data, RAMIN, RAMOUT, rom_1_data;

  Counter #(.width(5), .max('h1f)) counter_1 (
    .Q(counter_1_q), .clk(controlled_buffer_1_out), .clr(RESETALL));  // open: load, D, count, carry
  assign controlled_buffer_1_out = HLT ? 1'b0 : 1'bz;  // Controlled_Buffer controlled_buffer_1
  assign controlled_buffer_1_out = not_1_out ? CLK : 1'bz;  // Controlled_Buffer controlled_buffer_2
  not not_1 (not_1_out, HLT);
  not not_2 (not_2_out, STR);
  RAM #(.addrWidth(2)) ram_1 (.addr(RAMADDR), .data(ram_1_data), .clk(CLK), .ld(not_2_out));  // open: sel, clr
  Button button_1 (.out(RESETALL));
  not not_3 (not_3_out, STR);
  assign RAMOUT = not_3_out ? ram_1_data : 8'bz;  // Controlled_Buffer controlled_buffer_3
  assign ram_1_data = STR ? RAMIN : 8'bz;  // Controlled_Buffer controlled_buffer_4
  ROM #(.addrWidth(5)) rom_1 (.addr(counter_1_q), .data(rom_1_data));  // open: sel
  assign RAMOUT = STR ? {8{1'b0}} : 8'bz;  // Controlled_Buffer controlled_buffer_5
  Register INSTRUCTION_REGISTER (.D(rom_1_data), .clk(CLK));  // open: en, Q, clr
  Clock clock_1 (.out(CLK));
  CONTROL_UNIT CONTROL_UNIT (
    .INSTR(rom_1_data), .RDM(CONTROL_UNIT_rdm), .REGADDR0(CONTROL_UNIT_regaddr0),
    .REGADDR1(CONTROL_UNIT_regaddr1), .RAMADDR(RAMADDR), .STR(STR), .HLT(HLT), .ADD(CONTROL_UNIT_add),
    .MOVREG(CONTROL_UNIT_movreg), .MOVACC(CONTROL_UNIT_movacc));
  ALU ALU (
    .RDM(CONTROL_UNIT_rdm), .STR(STR), .ADD(CONTROL_UNIT_add), .CLK(CLK), .MOVREG(CONTROL_UNIT_movreg),
    .MOVACC(CONTROL_UNIT_movacc), .RAMOUT(RAMOUT), .REGADRR0(CONTROL_UNIT_regaddr0),
    .REGADRR1(CONTROL_UNIT_regaddr1), .RESETALL(RESETALL), .REGOUT(RAMIN));

  // Notes on the sheet:
  //   RAM
  //   ROM
  //   contents of rom_1 (hex, n*v repeats v):
  //   d0 d5 91 c0 b4 91 c0 e3 80
endmodule

module CONTROL_UNIT (
  input  [7:0] INSTR,
  output RDM,
  output [1:0] REGADDR0,
  output [1:0] REGADDR1,
  output [1:0] RAMADDR,
  output STR,
  output HLT,
  output ADD,
  output MOVREG,
  output MOVACC
);

  wire and_1_out, and_2_out, and_3_out, and_4_out, and_5_out, and_6_out, and_7_out, and_8_out, and_9_out,
       and_10_out, and_11_out, and_12_out, not_1_out, not_2_out, not_3_out, not_4_out, not_5_out, not_6_out,
       not_7_out, not_8_out, not_9_out, not_10_out;

  and and_1 (and_1_out, INSTR[7], INSTR[6]);
  and and_2 (and_2_out, INSTR[7], INSTR[6]);
  and and_3 (and_3_out, INSTR[7], not_1_out);
  not not_1 (not_1_out, INSTR[6]);
  and and_4 (and_4_out, INSTR[7], not_2_out);
  not not_2 (not_2_out, INSTR[6]);
  and and_5 (and_5_out, INSTR[7], not_3_out);
  not not_3 (not_3_out, INSTR[6]);
  and and_6 (and_6_out, INSTR[7], INSTR[6]);
  not not_4 (not_4_out, INSTR[5]);
  and and_7 (and_7_out, and_2_out, INSTR[5]);
  and and_8 (and_8_out, and_3_out, not_5_out);
  not not_5 (not_5_out, INSTR[5]);
  and and_9 (and_9_out, and_4_out, not_6_out);
  not not_6 (not_6_out, INSTR[5]);
  and and_10 (and_10_out, and_5_out, INSTR[5]);
  and and_11 (and_11_out, and_6_out, not_7_out);
  not not_7 (not_7_out, INSTR[5]);
  and and_12 (and_12_out, and_1_out, not_4_out);
  and and_13 (RDM, and_12_out, INSTR[4]);
  and and_14 (STR, and_7_out, not_8_out);
  not not_8 (not_8_out, INSTR[4]);
  and and_15 (HLT, and_8_out, not_9_out);
  not not_9 (not_9_out, INSTR[4]);
  and and_16 (ADD, and_9_out, INSTR[4]);
  and and_17 (MOVREG, and_10_out, INSTR[4]);
  and and_18 (MOVACC, and_11_out, not_10_out);
  not not_10 (not_10_out, INSTR[4]);
  assign REGADDR0 = ADD ? INSTR[3:2] : 2'bz;  // Controlled_Buffer controlled_buffer_1
  assign REGADDR1 = ADD ? INSTR[1:0] : 2'bz;  // Controlled_Buffer controlled_buffer_2
  assign REGADDR0 = STR ? INSTR[3:2] : 2'bz;  // Controlled_Buffer controlled_buffer_3
  assign REGADDR0 = RDM ? INSTR[3:2] : 2'bz;  // Controlled_Buffer controlled_buffer_4
  assign RAMADDR = STR ? INSTR[1:0] : 2'bz;  // Controlled_Buffer controlled_buffer_5
  assign RAMADDR = RDM ? INSTR[1:0] : 2'bz;  // Controlled_Buffer controlled_buffer_6
  assign REGADDR0 = MOVREG ? INSTR[3:2] : 2'bz;  // Controlled_Buffer controlled_buffer_7
  assign REGADDR0 = MOVACC ? INSTR[3:2] : 2'bz;  // Controlled_Buffer controlled_buffer_8
  assign REGADDR1 = MOVREG ? INSTR[1:0] : 2'bz;  // Controlled_Buffer controlled_buffer_9
endmodule

module ALU (
  input  RDM,
  input  STR,
  input  ADD,
  input  CLK,
  input  MOVREG,
  input  MOVACC,
  input  [7:0] RAMOUT,
  input  [1:0] REGADRR0,
  input  [1:0] REGADRR1,
  input  RESETALL,
  output [7:0] REGOUT
);

  wire ACCSEL0, ACCSEL1, ACCSEL2, ACCSEL3, and_1_out, and_2_out, and_3_out, and_4_out, and_5_out, and_6_out,
       and_7_out, and_8_out, and_9_out, and_10_out, and_11_out, and_12_out, and_13_out, and_14_out,
       and_15_out, and_16_out, not_1_out, not_2_out, not_3_out, not_4_out, not_5_out, not_6_out, not_7_out,
       not_8_out, not_9_out, not_10_out, not_11_out, not_12_out, not_13_out, not_14_out, not_15_out,
       not_16_out, not_17_out, not_18_out, or_1_out, or_2_out, or_3_out, or_4_out, or_5_out;
  wire [1:0] controlled_buffer_1_out, REGADDR1;
  wire [7:0] ACCOUT, controlled_buffer_4_out, controlled_buffer_12_out, controlled_buffer_24_out,
       controlled_buffer_36_out, controlled_buffer_41_out, controlled_buffer_45_out, REG00OUT, REG00OUT1,
       REG01OUT, REG01OUT1, REG10OUT, REG10OUT1, REG11OUT, REG11OUT1, REGIN, REGISTER0_q, REGISTER1_q,
       REGISTER2_q, REGISTER3_q, SUM;

  or or_1 (or_1_out, MOVREG, ADD);
  assign controlled_buffer_1_out = or_2_out ? REGADRR0 : 2'bz;  // Controlled_Buffer controlled_buffer_1
  or or_2 (or_2_out, MOVACC, or_3_out);
  or or_3 (or_3_out, MOVREG, or_4_out);
  not not_1 (not_1_out, MOVACC);
  or or_4 (or_4_out, ADD, or_5_out);
  not not_2 (not_2_out, MOVREG);
  or or_5 (or_5_out, STR, RDM);
  assign REGADDR1 = or_1_out ? REGADRR1 : 2'bz;  // Controlled_Buffer controlled_buffer_2
  assign REGADDR1 = not_3_out ? 2'b00 : 2'bz;  // Controlled_Buffer controlled_buffer_3
  not not_3 (not_3_out, or_1_out);
  assign controlled_buffer_4_out = and_7_out ? REGIN : 8'bz;  // Controlled_Buffer controlled_buffer_4
  and and_1 (and_1_out, and_7_out, RDM);
  assign controlled_buffer_4_out = and_1_out ? RAMOUT : 8'bz;  // Controlled_Buffer controlled_buffer_5
  assign controlled_buffer_4_out = ACCSEL0 ? ACCOUT : 8'bz;  // Controlled_Buffer controlled_buffer_6
  not not_4 (not_4_out, REGADDR1[0]);
  not not_5 (not_5_out, REGADDR1[1]);
  assign controlled_buffer_1_out = and_2_out ? 2'b00 : 2'bz;  // Controlled_Buffer controlled_buffer_7
  and and_2 (and_2_out, not_1_out, and_3_out);
  and and_3 (and_3_out, not_2_out, and_4_out);
  and and_4 (and_4_out, not_6_out, and_5_out);
  not not_6 (not_6_out, ADD);
  and and_5 (and_5_out, not_7_out, not_8_out);
  not not_7 (not_7_out, STR);
  not not_8 (not_8_out, RDM);
  Register REGISTER0 (.D(controlled_buffer_4_out), .Q(REGISTER0_q), .clk(CLK), .clr(RESETALL));  // open: en
  and and_6 (and_6_out, not_4_out, not_5_out);
  not not_9 (not_9_out, controlled_buffer_1_out[0]);
  not not_10 (not_10_out, controlled_buffer_1_out[1]);
  assign REG00OUT1 = and_7_out ? REGISTER0_q : 8'bz;  // Controlled_Buffer controlled_buffer_8
  assign REG00OUT = and_6_out ? REGISTER0_q : 8'bz;  // Controlled_Buffer controlled_buffer_9
  not not_11 (not_11_out, REGADDR1[1]);
  and and_7 (and_7_out, not_9_out, not_10_out);
  assign ACCSEL1 = and_10_out ? MOVACC : 1'bz;  // Controlled_Buffer controlled_buffer_10
  not not_12 (not_12_out, and_10_out);
  assign ACCSEL1 = not_12_out ? 1'b0 : 1'bz;  // Controlled_Buffer controlled_buffer_11
  assign controlled_buffer_12_out = and_10_out ? REGIN : 8'bz;  // Controlled_Buffer controlled_buffer_12
  and and_8 (and_8_out, and_10_out, RDM);
  assign controlled_buffer_12_out = and_8_out ? RAMOUT : 8'bz;  // Controlled_Buffer controlled_buffer_13
  assign controlled_buffer_12_out = ACCSEL1 ? ACCOUT : 8'bz;  // Controlled_Buffer controlled_buffer_14
  and and_9 (and_9_out, REGADDR1[0], not_11_out);
  assign REGIN = MOVREG ? REG00OUT : 8'bz;  // Controlled_Buffer controlled_buffer_15
  assign REGIN = MOVREG ? REG01OUT : 8'bz;  // Controlled_Buffer controlled_buffer_16
  and and_10 (and_10_out, controlled_buffer_1_out[0], not_13_out);
  not not_13 (not_13_out, controlled_buffer_1_out[1]);
  assign ACCSEL0 = not_14_out ? 1'b0 : 1'bz;  // Controlled_Buffer controlled_buffer_17
  assign ACCSEL0 = and_7_out ? MOVACC : 1'bz;  // Controlled_Buffer controlled_buffer_18
  not not_14 (not_14_out, and_7_out);
  assign REG01OUT1 = and_10_out ? REGISTER1_q : 8'bz;  // Controlled_Buffer controlled_buffer_19
  Register REGISTER1 (.D(controlled_buffer_12_out), .Q(REGISTER1_q), .clk(CLK), .clr(RESETALL));  // open: en
  assign REG01OUT = and_9_out ? REGISTER1_q : 8'bz;  // Controlled_Buffer controlled_buffer_20
  assign REGIN = MOVREG ? REG10OUT : 8'bz;  // Controlled_Buffer controlled_buffer_21
  assign REGIN = MOVREG ? REG11OUT : 8'bz;  // Controlled_Buffer controlled_buffer_22
  not not_15 (not_15_out, and_13_out);
  assign ACCSEL2 = not_15_out ? 1'b0 : 1'bz;  // Controlled_Buffer controlled_buffer_23
  assign controlled_buffer_24_out = and_13_out ? REGIN : 8'bz;  // Controlled_Buffer controlled_buffer_24
  and and_11 (and_11_out, and_13_out, RDM);
  assign controlled_buffer_24_out = and_11_out ? RAMOUT : 8'bz;  // Controlled_Buffer controlled_buffer_25
  assign controlled_buffer_24_out = ACCSEL2 ? ACCOUT : 8'bz;  // Controlled_Buffer controlled_buffer_26
  not not_16 (not_16_out, REGADDR1[0]);
  and and_12 (and_12_out, not_16_out, REGADDR1[1]);
  assign REGOUT = STR ? REG00OUT1 : 8'bz;  // Controlled_Buffer controlled_buffer_27
  assign REGOUT = STR ? REG01OUT1 : 8'bz;  // Controlled_Buffer controlled_buffer_28
  not not_17 (not_17_out, controlled_buffer_1_out[0]);
  and and_13 (and_13_out, not_17_out, controlled_buffer_1_out[1]);
  assign ACCSEL2 = and_13_out ? MOVACC : 1'bz;  // Controlled_Buffer controlled_buffer_29
  Register REGISTER2 (.D(controlled_buffer_24_out), .Q(REGISTER2_q), .clk(CLK), .clr(RESETALL));  // open: en
  assign REGOUT = STR ? REG10OUT1 : 8'bz;  // Controlled_Buffer controlled_buffer_30
  assign REGOUT = STR ? REG11OUT1 : 8'bz;  // Controlled_Buffer controlled_buffer_31
  and and_14 (and_14_out, controlled_buffer_1_out[1], controlled_buffer_1_out[0]);
  assign REG10OUT1 = and_13_out ? REGISTER2_q : 8'bz;  // Controlled_Buffer controlled_buffer_32
  assign REG10OUT = and_12_out ? REGISTER2_q : 8'bz;  // Controlled_Buffer controlled_buffer_33
  assign ACCSEL3 = and_14_out ? MOVACC : 1'bz;  // Controlled_Buffer controlled_buffer_34
  not not_18 (not_18_out, and_14_out);
  assign ACCSEL3 = not_18_out ? 1'b0 : 1'bz;  // Controlled_Buffer controlled_buffer_35
  assign controlled_buffer_36_out = and_14_out ? REGIN : 8'bz;  // Controlled_Buffer controlled_buffer_36
  and and_15 (and_15_out, and_14_out, RDM);
  assign controlled_buffer_36_out = and_15_out ? RAMOUT : 8'bz;  // Controlled_Buffer controlled_buffer_37
  assign controlled_buffer_36_out = ACCSEL3 ? ACCOUT : 8'bz;  // Controlled_Buffer controlled_buffer_38
  and and_16 (and_16_out, REGADDR1[0], REGADDR1[1]);
  assign REG11OUT1 = and_14_out ? REGISTER3_q : 8'bz;  // Controlled_Buffer controlled_buffer_39
  Register REGISTER3 (.D(controlled_buffer_36_out), .Q(REGISTER3_q), .clk(CLK), .clr(RESETALL));  // open: en
  assign REG11OUT = and_16_out ? REGISTER3_q : 8'bz;  // Controlled_Buffer controlled_buffer_40
  assign controlled_buffer_41_out = ADD ? REG00OUT : 8'bz;  // Controlled_Buffer controlled_buffer_41
  assign controlled_buffer_41_out = ADD ? REG01OUT : 8'bz;  // Controlled_Buffer controlled_buffer_42
  assign controlled_buffer_41_out = ADD ? REG10OUT : 8'bz;  // Controlled_Buffer controlled_buffer_43
  assign controlled_buffer_41_out = ADD ? REG11OUT : 8'bz;  // Controlled_Buffer controlled_buffer_44
  assign controlled_buffer_45_out = ADD ? REG00OUT1 : 8'bz;  // Controlled_Buffer controlled_buffer_45
  assign controlled_buffer_45_out = ADD ? REG01OUT1 : 8'bz;  // Controlled_Buffer controlled_buffer_46
  assign controlled_buffer_45_out = ADD ? REG10OUT1 : 8'bz;  // Controlled_Buffer controlled_buffer_47
  assign controlled_buffer_45_out = ADD ? REG11OUT1 : 8'bz;  // Controlled_Buffer controlled_buffer_48
  Adder adder_1 (.a(controlled_buffer_41_out), .b(controlled_buffer_45_out), .out(SUM));  // open: cin, cout
  Register ACUMULATOR (.D(SUM), .Q(ACCOUT), .clk(CLK), .clr(RESETALL));  // open: en
endmodule
